# Fritzing sketch CapacitivSensor (saved by Fritzing 0.9.0b)
breadboards: 1

parts:
  Part1 = Arduino Uno (Rev3)
  R1 = Resistor [tolerance=±5% resistance=1M package="1206 [SMD]"]
  R2 = Resistor [tolerance=±5% resistance=1M package="1206 [SMD]"]
  R3 = Resistor [tolerance=±5% resistance=1M package="1206 [SMD]"]
  R4 = Resistor [tolerance=±5% resistance=1M package="1206 [SMD]"]
  R5 = Resistor [tolerance=±5% resistance=1M package="1206 [SMD]"]
  R6 = Resistor [tolerance=±5% resistance=1M package="1206 [SMD]"]
  R7 = Resistor [tolerance=±5% resistance=1M package="1206 [SMD]"]
  R8 = Resistor [tolerance=±5% resistance=1M package="1206 [SMD]"]
  R9 = Resistor [tolerance=±5% resistance=1M package="1206 [SMD]"]
  R10 = Resistor [tolerance=±5% resistance=1M package="1206 [SMD]"]
  R11 = Resistor [tolerance=±5% resistance=1k package="1206 [SMD]"]

nets:
  N1: Part1.D2, R11.Pin_0
  N2: Part1.D4, R1.Pin_0
  N3: R1.Pin_1, R2.Pin_0
  N4: R2.Pin_1, R3.Pin_0
  N5: R3.Pin_1, R4.Pin_0
  N6: R4.Pin_1, R5.Pin_0
  N7: R5.Pin_1, R6.Pin_0
  N8: R6.Pin_1, R7.Pin_0
  N9: R7.Pin_1, R8.Pin_1
  N10: R8.Pin_0, R9.Pin_0
  N11: R9.Pin_1, R10.Pin_0

notes:
  Aluminium/Copper Foil or something like that
