# Fritzing sketch knock (saved by Fritzing 0.9.0b)
breadboards: 1

parts:
  Arduino_Uno = Arduino Uno (Rev3)
  J1 = Piezo Speaker
  R1 = Resistor [tolerance=±5% resistance=10k package="0805 [SMD]"]

nets:
  N1: Arduino_Uno.A0, J1.pin2, R1.Pin_1
  N2: Arduino_Uno.GND, J1.pin1, R1.Pin_0
